# Fritzing sketch Dht11_board (saved by Fritzing 0.9.4)
circuit board: 2.12309cm x 2.86163cm

parts:
  DHT1 = DHT11 Humitidy and Temperature Sensor
  R1 = Resistor [tolerance=±5% resistance=220 package="0603 [SMD]"]
  JP1 = Header 3 [package=screwterminal-3.5mm-3_lock.007s]

nets:
  N1: DHT1.VDD, R1.Pin_0, JP1.1
  N2: DHT1.DATA, R1.Pin_1, JP1.2
  N3: DHT1.GND, JP1.3

custom parts:
  DHT11 Humitidy and Temperature Sensor: DHT11 Humidity and Temperature Sensor
